# Fritzing sketch 555-Mosfet-9V (saved by Fritzing 0.9.3b)
breadboards: 1

parts:
  JP2 = Header 2 [package=molex-1x2_lock]
  BAT1 = BC9VPC [package=bc9vpc]
  BAT2 = BC9VPC [package=bc9vpc]
  BAT3 = BC9VPC [package=bc9vpc]
  BAT4 = BC9VPC [package=bc9vpc]
  R10 = Resistor [tolerance=±5% resistance=1k package="2512 [SMD]"]
  P3 = S1133 Si Photodiode [part_number=TIL78 package="8mm Ceramic [THT]"]
  LD7 = LD [part_number=TIL32]
  R14 = Resistor [tolerance=±5% resistance=47k package="2512 [SMD]"]
  R25 = Resistor [tolerance=±5% resistance=680 package="2512 [SMD]"]
  U1 = 555 Timer [package="DIP8 [THT]"]
  C1 = Ceramic Capacitor [capacitance=10nF voltage=50V package="100 mil [THT, multilayer]"]
  U3 = POT [part_number=B50K package=pot_mammoth]
  R30 = Resistor [tolerance=±5% resistance=470k package="2512 [SMD]"]
  C3 = Ceramic Capacitor [capacitance=1nF voltage=50V package="100 mil [THT, multilayer]"]
  Q5 = TRANSISTOR_NPN [part_number=2222 package=to-92]
  R31 = Resistor [tolerance=±5% resistance=4.7k package="2512 [SMD]"]
  U5 = DIODE-ZENER [part_number=1N5388 package=diode-zener]
  U6 = DIODE-ZENER [part_number=1N5388 package=diode-zener]
  Q6 = Basic FET N-Channel [part_number=IRF830 package="DPak [SMD]"]
  BAT5 = BC9VPC [package=bc9vpc]
  Q7 = Basic FET N-Channel [part_number=IRF830 package="DPak [SMD]"]
  Q8 = TRANSISTOR_PNP [part_number=3906 package=to-92]
  R32 = Resistor [tolerance=±5% resistance=4.7 package="2512 [SMD]"]
  C4 = Electrolytic Capacitor [capacitance=10µF voltage=50V package="0405 [SMD, electrolytic]"]
  U7 = DIODE-ZENER [part_number=1N5388 package=diode-zener]
  U8 = DIODE-ZENER [part_number=1N5388 package=diode-zener]

nets:
  N1: JP2.1, BAT1.V+, U8.C
  N2: JP2.2, U6.C, Q6.drain
  N3: BAT1.V-, BAT2.V+
  N4: BAT2.V-, BAT3.V+
  N5: BAT3.V-, BAT4.V+
  N6: BAT4.V-, Q7.drain
  N7: R10.Pin_0, U1.Trigger, U1.Threshold, C3.1
  N8: R10.Pin_1, U3.E
  N9: P3.cathode, R30.Pin_0, R31.Pin_0
  N10: P3.anode, U1.Output
  N11: LD7.cathode, U1.Ground, C1.1, R30.Pin_1, C3.0, Q6.source, BAT5.V-, Q7.source, Q8.C, C4.-
  N12: LD7.anode, R25.Pin_0
  N13: R14.Pin_0, R25.Pin_1, U1.Reset, U1.Vcc_Supply_Voltage, Q5.C, BAT5.V+, C4.+
  N14: R14.Pin_1, U1.Discharge, U3.A
  N15: U1.Control_Voltage, C1.0
  N16: Q5.E, Q8.E, R32.Pin_0
  N17: Q5.B, R31.Pin_1, Q8.B
  N18: U5.C, U8.A
  N19: U5.A, U7.A
  N20: U6.A, U7.C
  N21: Q6.Gate, Q7.Gate, R32.Pin_1

custom parts:
  LD: A Generic Red Dot Laser Diode Module (~5mW)
